// Logisim project Nano8.circ as structural Verilog
module main (
);

  wire CLK, DOUBLE, REG_IE, REG_OE, RES;
  wire [2:0] REG_ISEL, REG_OSEL;
  wire [7:0] DATA0, DATA1;

  Registers registers_1 (
    .D(DOUBLE), .OE(REG_OE), .RES(RES), .CLK(CLK), .P0(DATA0), .IE(REG_IE), .ISEL(REG_ISEL), .OSEL(REG_OSEL),
    .P1(DATA0), .P2(DATA1));
endmodule

module Registers (
  input  D,
  input  OE,
  input  RES,
  input  CLK,
  input  [7:0] P0,
  input  IE,
  input  [2:0] ISEL,
  input  [2:0] OSEL,
  output [7:0] P1,
  output [7:0] P2
);

  wire demultiplexer_1_out0, demultiplexer_1_out1, demultiplexer_1_out2, demultiplexer_1_out3,
       demultiplexer_1_out4, demultiplexer_1_out5, demultiplexer_1_out6, demultiplexer_1_out7,
       demultiplexer_2_out0, demultiplexer_2_out1, demultiplexer_2_out2, demultiplexer_2_out3,
       demultiplexer_2_out4, demultiplexer_2_out5, demultiplexer_2_out6, demultiplexer_2_out7, E1E, E2E, O1E,
       O2E, ODD, xor_1_out, xor_2_out, xor_3_out, xor_4_out, xor_5_out, xor_6_out, xor_7_out, xor_8_out;
  wire [7:0] controlled_buffer_1_out, controlled_buffer_5_out, register_4_q, register_5_q, register_6_q,
       register_7_q, register_8_q, register_9_q, register_10_q, register_11_q;

  Register #(.trigger("high"), .width(1)) register_1 (.D(D), .en(1'b1), .clk(1'b1), .clr(1'b0));  // open: Q
  Register #(.trigger("high"), .width(3)) register_2 (.D(ISEL), .en(1'b1), .clk(1'b1), .clr(1'b0));  // open: Q
  Register #(.trigger("high"), .width(1)) register_3 (.D(IE), .en(1'b1), .clk(1'b1), .clr(1'b0));  // open: Q
  not not_1 (ODD, ISEL[0]);
  Demultiplexer #(.select(3)) demultiplexer_1 (
    .out0(demultiplexer_1_out0), .out1(demultiplexer_1_out1), .out2(demultiplexer_1_out2),
    .out3(demultiplexer_1_out3), .out4(demultiplexer_1_out4), .out5(demultiplexer_1_out5),
    .out6(demultiplexer_1_out6), .out7(demultiplexer_1_out7), .in(IE), .sel(ISEL));
  and and_1 (E1E, ODD, ISEL[0]);
  and and_2 (O1E, ISEL[0], ISEL[0]);
  Register register_4 (.D(P0), .en(demultiplexer_1_out0), .clk(CLK), .Q(register_4_q), .clr(RES));
  Register register_5 (.D(P0), .en(demultiplexer_1_out1), .clk(CLK), .Q(register_5_q), .clr(RES));
  Register register_6 (.D(P0), .en(demultiplexer_1_out2), .clk(RES), .Q(register_6_q), .clr(RES));
  Register register_7 (.D(P0), .en(demultiplexer_1_out3), .clk(CLK), .Q(register_7_q), .clr(RES));
  Register register_8 (.D(P0), .en(demultiplexer_1_out4), .clk(CLK), .Q(register_8_q), .clr(RES));
  Register register_9 (.D(P0), .en(demultiplexer_1_out5), .clk(CLK), .Q(register_9_q), .clr(RES));
  Register register_10 (.D(P0), .en(demultiplexer_1_out6), .clk(CLK), .Q(register_10_q), .clr(RES));
  Register register_11 (.D(P0), .en(demultiplexer_1_out7), .clk(CLK), .Q(register_11_q), .clr(RES));
  Register #(.trigger("high"), .width(1)) register_12 (.D(CLK), .en(1'b1), .clk(1'b1), .clr(1'b0));  // open: Q
  Register #(.trigger("high")) register_13 (.D(P0), .en(1'b1), .clk(1'b1), .clr(1'b0));  // open: Q
  and and_3 (E2E, D, ISEL[0], ISEL[0]);
  and and_4 (O2E, ~D, ISEL[0], ODD);  // AND_Gate
  assign controlled_buffer_1_out = xor_2_out ? register_5_q : 8'bz;  // Controlled_Buffer controlled_buffer_1
  assign controlled_buffer_1_out = xor_4_out ? register_7_q : 8'bz;  // Controlled_Buffer controlled_buffer_2
  assign controlled_buffer_1_out = xor_6_out ? register_9_q : 8'bz;  // Controlled_Buffer controlled_buffer_3
  assign controlled_buffer_1_out = xor_8_out ? register_11_q : 8'bz;  // Controlled_Buffer controlled_buffer_4
  assign controlled_buffer_5_out = xor_1_out ? register_4_q : 8'bz;  // Controlled_Buffer controlled_buffer_5
  xor xor_1 (xor_1_out, demultiplexer_2_out0, demultiplexer_2_out7);
  xor xor_2 (xor_2_out, demultiplexer_2_out1, demultiplexer_2_out0);
  assign controlled_buffer_5_out = xor_3_out ? register_6_q : 8'bz;  // Controlled_Buffer controlled_buffer_6
  xor xor_3 (xor_3_out, demultiplexer_2_out2, demultiplexer_2_out1);
  xor xor_4 (xor_4_out, demultiplexer_2_out3, demultiplexer_2_out2);
  assign controlled_buffer_5_out = xor_5_out ? register_8_q : 8'bz;  // Controlled_Buffer controlled_buffer_7
  xor xor_5 (xor_5_out, demultiplexer_2_out4, demultiplexer_2_out3);
  xor xor_6 (xor_6_out, demultiplexer_2_out5, demultiplexer_2_out4);
  assign controlled_buffer_5_out = xor_7_out ? register_10_q : 8'bz;  // Controlled_Buffer controlled_buffer_8
  xor xor_7 (xor_7_out, demultiplexer_2_out6, demultiplexer_2_out5);
  xor xor_8 (xor_8_out, demultiplexer_2_out6, demultiplexer_2_out7);
  Register #(.trigger("high"), .width(1)) register_14 (.D(RES), .en(1'b1), .clk(1'b1), .clr(1'b0));  // open: Q
  assign P1 = E1E ? controlled_buffer_5_out : 8'bz;  // Controlled_Buffer controlled_buffer_9
  assign P1 = O1E ? controlled_buffer_1_out : 8'bz;  // Controlled_Buffer controlled_buffer_10
  assign P2 = E2E ? controlled_buffer_5_out : 8'bz;  // Controlled_Buffer controlled_buffer_11
  assign P2 = O2E ? controlled_buffer_1_out : 8'bz;  // Controlled_Buffer controlled_buffer_12
  Register #(.trigger("high")) register_15 (.D(P1), .en(1'b1), .clk(1'b1), .clr(1'b0));  // open: Q
  Register #(.trigger("high")) register_16 (.D(P2), .en(1'b1), .clk(1'b1), .clr(1'b0));  // open: Q
  Demultiplexer #(.select(3)) demultiplexer_2 (
    .out0(demultiplexer_2_out0), .out1(demultiplexer_2_out1), .out2(demultiplexer_2_out2),
    .out3(demultiplexer_2_out3), .out4(demultiplexer_2_out4), .out5(demultiplexer_2_out5),
    .out6(demultiplexer_2_out6), .out7(demultiplexer_2_out7), .in(ISEL[0]), .sel(OSEL));
  Register #(.trigger("high"), .width(3)) register_17 (.D(OSEL), .en(1'b1), .clk(1'b1), .clr(1'b0));  // open: Q
  Register #(.trigger("high"), .width(1)) register_18 (.D(ISEL[0]), .en(1'b1), .clk(1'b1), .clr(1'b0));  // open: Q

  assign OE = ISEL[0];

  // Other names for the same wires on the sheet: EVEN = ISEL[0]
endmodule
